// Digital circuit SOP.dig as structural Verilog
module SOP (
  input  A,
  input  B,
  input  C,
  input  D,
  output Y
);

  wire and_1_out, and_2_out, and_3_out;

  not not_1 (A, A);
  not not_2 (A, B);
  not not_3 (A, C);
  not not_4 (A, A);
  and and_1 (and_1_out, A, A);
  and and_2 (and_2_out, A, A);
  and and_3 (and_3_out, A, A);
  or or_1 (Y, and_2_out, and_3_out);

  assign D = A;

  // Notes on the sheet:
  //   A: MSB
  //   D: LSB
  //   Use A as the most-significant bit and 
  //   D as the least-significant bit.
endmodule

/* Test case:
A B C D Y
0 0 0 0 X
0 0 0 1 1
*/
